// Logisim project Ctl_Shift_Add_Sub_Mov.circ as structural Verilog: 2 circuits, main circuit Shift_Add_Sub_Mov
module Shift_Add_Sub_Mov (
  input  Enable,
  input  [15:0] Instruction,
  output [3:0] Flags_Update_Mask,
  output Carry,
  output Imm32_Enable,
  output [2:0] Rm,
  output [2:0] Rn,
  output [2:0] Rd,
  output [4:0] Imm5,
  output [31:0] Imm32,
  output [3:0] ALU_Opcode
);

  wire [4:0] bitselector_2_out;
  wire [8:0] bitselector_1_out;

  BitSelector #(.group(9), .width(16)) bitselector_1 (.in(Instruction), .out(bitselector_1_out), .sel(1'b1));
  BitSelector #(.group(5), .width(9)) bitselector_2 (.in(bitselector_1_out), .out(bitselector_2_out), .sel(1'b0));
  table_de_verite table_de_verite_1 (.opcode(bitselector_2_out), .codop(ALU_Opcode));
  Transistor #(.\type ("n"), .width(4)) transistor_1 (.in(Imm5[3:0]), .out(bitselector_2_out[3:0]));  // open: gate
  // Pins of 4 and 5 bits meet at Imm5
  // Pins of 4 and 5 bits meet at bitselector_2_out

  // Notes on the sheet:
  //   Note: ALU uses Rn register for shifts. Use Rn instead of Rm for shifts (immediate) here too
  //   Note 3: Imm32_Enable forces the use of the immediate for Rm register
  //   Note 2: MOV uses RSB ALU opcode with Imm8 reversed so that it is copied to output register
  //   Pull output low on Enable = 0
  //   only ADD and SUB use Rm
  //   Enable carry for SUB since it is reversed in ALU
  //   ALU will use Imm32 instead of Rm
endmodule

module table_de_verite (
  input  [4:0] opcode,
  output [3:0] codop
);

  wire not_1_out;

  not not_1 (not_1_out, opcode[4]);
  not not_2 (codop[1], opcode[3]);
  and and_1 (codop[0], not_1_out, opcode[2]);

  assign codop[3:2] = opcode[4:3];
endmodule
